// Logisim project cpu.circ as structural Verilog: 14 circuits, main circuit main
module OPDEC (
  input  imm,
  input  op0,
  input  op1,
  input  op2,
  input  op3,
  input  op4,
  output alu0,
  output alu1,
  output memlen0,
  output memlen1,
  output memtype,
  output br0,
  output br1,
  output br2
);

  wire and_1_out, and_2_out, and_3_out, and_4_out, and_5_out, and_6_out, and_7_out, and_8_out, and_9_out,
       and_10_out, and_11_out, and_12_out, and_13_out, and_14_out, and_15_out, and_16_out, and_17_out,
       and_18_out, and_19_out, and_20_out, and_21_out, and_22_out, and_23_out, and_24_out, and_25_out,
       and_26_out, and_27_out, and_28_out, and_29_out, and_30_out, and_31_out, and_32_out, and_33_out,
       and_34_out, and_35_out, and_36_out, and_37_out, and_38_out, and_39_out, and_40_out, and_41_out,
       and_42_out, and_43_out, and_44_out, and_45_out, and_46_out, and_47_out, and_48_out, and_49_out,
       and_50_out, and_51_out, and_52_out, and_53_out, and_54_out, and_55_out, and_56_out, not_1_out,
       not_2_out, not_3_out, not_4_out, not_5_out, not_6_out, not_7_out, not_8_out, not_9_out, not_10_out,
       not_11_out, not_12_out, not_13_out, not_14_out, not_15_out, not_16_out, not_17_out, not_18_out,
       not_19_out, not_20_out, not_21_out, not_22_out, not_23_out, not_24_out, not_25_out, not_26_out,
       not_27_out, not_28_out, not_29_out, not_30_out, not_31_out, not_32_out, not_33_out, not_34_out,
       not_35_out, not_36_out, not_37_out, not_38_out, not_39_out, not_40_out, not_41_out, not_42_out,
       not_43_out, not_44_out, not_45_out, not_46_out, not_47_out, not_48_out, not_49_out, not_50_out,
       not_51_out, not_52_out, not_53_out, not_54_out, not_55_out, not_56_out, not_57_out, not_58_out,
       not_59_out, not_60_out, not_61_out, not_62_out, not_63_out, not_64_out, not_65_out, not_66_out,
       not_67_out, not_68_out, not_69_out, not_70_out, not_71_out, not_72_out, not_73_out, not_74_out,
       not_75_out, not_76_out, not_77_out, not_78_out, not_79_out, not_80_out, not_81_out, not_82_out,
       not_83_out, not_84_out, not_85_out, not_86_out, not_87_out, not_88_out;

  not not_1 (not_1_out, imm);
  not not_2 (not_2_out, op1);
  not not_3 (not_3_out, op0);
  not not_4 (not_4_out, op3);
  not not_5 (not_5_out, op4);
  not not_6 (not_6_out, op0);
  not not_7 (not_7_out, op2);
  not not_8 (not_8_out, imm);
  not not_9 (not_9_out, op1);
  not not_10 (not_10_out, op2);
  not not_11 (not_11_out, op3);
  not not_12 (not_12_out, op4);
  not not_13 (not_13_out, op1);
  not not_14 (not_14_out, op1);
  not not_15 (not_15_out, op4);
  not not_16 (not_16_out, op4);
  not not_17 (not_17_out, imm);
  not not_18 (not_18_out, op2);
  not not_19 (not_19_out, imm);
  not not_20 (not_20_out, op1);
  not not_21 (not_21_out, op0);
  not not_22 (not_22_out, op3);
  not not_23 (not_23_out, op4);
  not not_24 (not_24_out, op0);
  not not_25 (not_25_out, op2);
  not not_26 (not_26_out, imm);
  not not_27 (not_27_out, op3);
  not not_28 (not_28_out, imm);
  not not_29 (not_29_out, op1);
  not not_30 (not_30_out, imm);
  not not_31 (not_31_out, op1);
  not not_32 (not_32_out, op1);
  not not_33 (not_33_out, op4);
  not not_34 (not_34_out, op2);
  not not_35 (not_35_out, op3);
  not not_36 (not_36_out, op4);
  not not_37 (not_37_out, op4);
  not not_38 (not_38_out, op0);
  not not_39 (not_39_out, op1);
  not not_40 (not_40_out, op4);
  not not_41 (not_41_out, op2);
  not not_42 (not_42_out, op0);
  not not_43 (not_43_out, op2);
  not not_44 (not_44_out, op3);
  not not_45 (not_45_out, op0);
  not not_46 (not_46_out, op1);
  not not_47 (not_47_out, op1);
  not not_48 (not_48_out, op2);
  not not_49 (not_49_out, op0);
  not not_50 (not_50_out, op3);
  not not_51 (not_51_out, op0);
  not not_52 (not_52_out, op1);
  not not_53 (not_53_out, op2);
  not not_54 (not_54_out, op3);
  not not_55 (not_55_out, op1);
  not not_56 (not_56_out, op4);
  not not_57 (not_57_out, op3);
  not not_58 (not_58_out, imm);
  not not_59 (not_59_out, op2);
  not not_60 (not_60_out, op3);
  not not_61 (not_61_out, op4);
  not not_62 (not_62_out, imm);
  not not_63 (not_63_out, op4);
  not not_64 (not_64_out, imm);
  not not_65 (not_65_out, op2);
  not not_66 (not_66_out, op3);
  not not_67 (not_67_out, imm);
  not not_68 (not_68_out, op2);
  not not_69 (not_69_out, op3);
  not not_70 (not_70_out, op4);
  not not_71 (not_71_out, op1);
  not not_72 (not_72_out, op4);
  not not_73 (not_73_out, imm);
  not not_74 (not_74_out, op3);
  not not_75 (not_75_out, op2);
  not not_76 (not_76_out, op1);
  not not_77 (not_77_out, op2);
  not not_78 (not_78_out, op3);
  not not_79 (not_79_out, op4);
  not not_80 (not_80_out, imm);
  not not_81 (not_81_out, op4);
  not not_82 (not_82_out, imm);
  not not_83 (not_83_out, op2);
  not not_84 (not_84_out, op3);
  and and_1 (and_1_out, not_1_out, not_2_out, op3, op4);
  and and_2 (and_2_out, not_3_out, op2, not_4_out, not_5_out);
  and and_3 (and_3_out, not_6_out, op1, not_7_out, op3);
  and and_4 (and_4_out, not_8_out, op0, not_9_out);
  and and_5 (and_5_out, op0, not_10_out, not_11_out, not_12_out);
  and and_6 (and_6_out, op0, not_13_out, op3, op4);
  and and_7 (and_7_out, op0, not_14_out, op2, not_15_out);
  and and_8 (and_8_out, op0, op2, op3, not_16_out);
  and and_9 (and_9_out, not_17_out, not_18_out, op3);
  and and_10 (and_10_out, not_19_out, not_20_out, op3, op4);
  and and_11 (and_11_out, not_21_out, op2, not_22_out, not_23_out);
  and and_12 (and_12_out, not_24_out, op1, not_25_out, op3);
  and and_13 (and_13_out, not_26_out, op1, op2, not_27_out);
  and and_14 (and_14_out, not_28_out, op0, not_29_out);
  and and_15 (and_15_out, not_30_out, op0, op4);
  and and_16 (and_16_out, op0, not_31_out, op3, op4);
  and and_17 (and_17_out, op0, not_32_out, op2, not_33_out);
  and and_18 (and_18_out, imm, op0, not_34_out, not_35_out, not_36_out);
  and and_19 (and_19_out, imm, op0, op2, op3, not_37_out);
  and and_20 (and_20_out, not_38_out, not_39_out, not_40_out);
  not not_85 (not_85_out, op3);
  and and_21 (and_21_out, op1, op2);
  and and_22 (and_22_out, op0, not_41_out);
  and and_23 (and_23_out, op0, op4);
  and and_24 (and_24_out, not_42_out, not_43_out, not_44_out);
  and and_25 (and_25_out, not_45_out, not_46_out, op3);
  and and_26 (and_26_out, not_47_out, not_48_out, op3);
  and and_27 (and_27_out, not_49_out, op2, op3);
  and and_28 (and_28_out, op0, op2, not_50_out);
  and and_29 (and_29_out, op0, op1);
  and and_30 (and_30_out, not_51_out, not_52_out, not_53_out);
  and and_31 (and_31_out, not_54_out, op4);
  and and_32 (and_32_out, not_55_out, op3, not_56_out);
  and and_33 (and_33_out, op1, not_57_out);
  and and_34 (and_34_out, op1, op2);
  and and_35 (and_35_out, op0, op3);
  and and_36 (and_36_out, op0, op2);
  and and_37 (and_37_out, not_58_out, not_59_out, not_60_out, not_61_out);
  not not_86 (not_86_out, op0);
  and and_38 (and_38_out, not_62_out, op2, op3, not_63_out);
  and and_39 (and_39_out, not_64_out, op1);
  and and_40 (and_40_out, op1, op3);
  and and_41 (and_41_out, imm, op4);
  and and_42 (and_42_out, imm, not_65_out, op3);
  and and_43 (and_43_out, imm, op2, not_66_out);
  and and_44 (and_44_out, not_67_out, not_68_out, not_69_out, not_70_out);
  not not_87 (not_87_out, op0);
  and and_45 (and_45_out, not_71_out, op2, op3, not_72_out);
  and and_46 (and_46_out, not_73_out, op1);
  and and_47 (and_47_out, op1, not_74_out);
  and and_48 (and_48_out, imm, op4);
  and and_49 (and_49_out, imm, not_75_out, op3);
  and and_50 (and_50_out, imm, not_76_out, op2);
  not not_88 (not_88_out, op0);
  and and_51 (and_51_out, not_77_out, not_78_out, not_79_out);
  and and_52 (and_52_out, not_80_out, op2, op3, not_81_out);
  and and_53 (and_53_out, not_82_out, op1);
  and and_54 (and_54_out, imm, not_83_out);
  and and_55 (and_55_out, imm, not_84_out);
  and and_56 (and_56_out, imm, op4);
  or or_1 (alu0, and_1_out, and_2_out, and_3_out, and_4_out, and_5_out, and_6_out, and_7_out, and_8_out);
  or or_2 (alu1, and_9_out, and_10_out, and_11_out, and_12_out, and_13_out, and_14_out, and_15_out, and_16_out, and_17_out, and_18_out, and_19_out);
  or or_3 (memlen0, and_20_out, not_85_out, and_21_out, and_22_out, and_23_out, imm);
  or or_4 (memlen1, and_24_out, op4, and_25_out, and_26_out, and_27_out, and_28_out, and_29_out, imm);
  or or_5 (memtype, and_30_out, and_31_out, and_32_out, and_33_out, and_34_out, and_35_out, and_36_out, imm);
  or or_6 (br0, and_37_out, not_86_out, and_38_out, and_39_out, and_40_out, and_41_out, and_42_out, and_43_out);
  or or_7 (br1, and_44_out, not_87_out, and_45_out, and_46_out, and_47_out, and_48_out, and_49_out, and_50_out);
  or or_8 (br2, not_88_out, and_51_out, and_52_out, and_53_out, and_54_out, and_55_out, and_56_out);
endmodule

module FSM (
  input  [15:0] IN,
  input  CLK,
  input  RST,
  output [31:0] OUT,
  output ERROR
);

  wire BRANCH_branch, nand_1_out, nand_2_out, nand_3_out, pull_resistor_2_node;
  wire [1:0] OPDEC_alu0;
  wire [2:0] controlled_buffer_1_out, OPDEC_br2, OPDEC_memtype, State_bis_q, State_bis_q_2;
  wire [6:0] multiplexer_1_out, State_q;
  wire [6:3] TRANS_ad0;
  wire [6:6] State_bis_q_3;

  OPDEC OPDEC (
    .imm(IN[15]), .op0(IN[14]), .op1(IN[13]), .op2(IN[12]), .op3(IN[11]), .op4(IN[10]), .alu0(OPDEC_alu0[0]),
    .alu1(OPDEC_alu0[1]), .memlen0(OPDEC_memtype[2]), .memlen1(OPDEC_memtype[1]), .memtype(OPDEC_memtype[0]),
    .br0(OPDEC_br2[2]), .br1(OPDEC_br2[1]), .br2(OPDEC_br2[0]));
  BRANCH BRANCH (
    .op2(IN[12]), .op3(IN[11]), .op4(IN[10]), .sta0(IN[0]), .sta1(IN[1]), .sta2(IN[2]), .branch(BRANCH_branch));
  assign controlled_buffer_1_out = nand_1_out ? {IN[15], OPDEC_alu0} : 3'bz;  // Controlled_Buffer controlled_buffer_1
  nand nand_1 (nand_1_out, OPDEC_alu0[0], OPDEC_alu0[1]);
  nand nand_2 (nand_2_out, OPDEC_memtype[2], OPDEC_memtype[1], OPDEC_memtype[0]);
  nand nand_3 (nand_3_out, OPDEC_br2[2], OPDEC_br2[1], OPDEC_br2[0]);
  assign controlled_buffer_1_out = nand_2_out ? OPDEC_memtype : 3'bz;  // Controlled_Buffer controlled_buffer_2
  assign controlled_buffer_1_out = nand_3_out ? OPDEC_br2 : 3'bz;  // Controlled_Buffer controlled_buffer_3
  TRANS TRANS (
    .IS_ALU(nand_1_out), .IS_MEM(nand_2_out), .IS_BRANCH(nand_3_out), .BRANCH(BRANCH_branch),
    .ad0(TRANS_ad0[3]), .ad1(TRANS_ad0[4]), .ad2(TRANS_ad0[5]), .ad3(TRANS_ad0[6]), .error(ERROR));
  // Probe on multiplexer_1_out
  Register #(.width(7)) State (.D(multiplexer_1_out), .en(1'b1), .Q(State_q), .clk(CLK), .clr(RST));
  Multiplexer #(.select(3), .width(7), .enable("false")) multiplexer_1 (
    .in0(7'b0001000), .in1({TRANS_ad0, controlled_buffer_1_out}), .in2({7{1'b0}}), .in3({7{1'b0}}),
    .in4({7{1'b0}}), .in5({7{1'b0}}), .out(multiplexer_1_out), .sel(State_bis_q_2));  // open: in6, in7
  Register #(.width(7), .trigger("falling")) State_bis (
    .D(State_q), .en(1'b1), .Q({State_bis_q_3[6], State_bis_q_2, State_bis_q}), .clk(CLK), .clr(RST));
  Pull_Resistor pull_resistor_1 (.node(RST));
  ROM #(.addrWidth(7), .dataWidth(32)) rom_1 (
    .addr({State_bis_q_3[6], State_bis_q_2, State_bis_q}), .data(OUT), .sel(pull_resistor_2_node));
  Pull_Resistor #(.pull(1)) pull_resistor_2 (.node(pull_resistor_2_node));

  // Other names for the same wires on the sheet: IMM = IN[15]

  // Notes on the sheet:
  //   OP0 is MSB
  //   IS_ALU
  //   IS_MEM
  //   IS_BRANCH
  //   fsm.rom
  //   micro instructions of control FSM
  //   contents of rom_1 (hex, n*v repeats v):
  //   48000000 7*0 82000000 7*0 6000015 6000016 7000015 0 6000010 0 0 0 f000505 33000501 f001505 33001501
  //   f002505 33002501 10*0 81800481 80000040 84000068 80800483 848004ab
endmodule

module REG4 (
  input  [1:0] RSEL2,
  input  WE,
  input  [1:0] RSEL1,
  input  [1:0] WSEL,
  input  [31:0] DATAIN,
  input  CLK,
  input  RST,
  output [31:0] DATAOUT1,
  output [31:0] DATAOUT2
);

  wire decoder_1_out0, decoder_1_out1, decoder_1_out2, decoder_1_out3;
  wire [31:0] multiplexer_1_out, multiplexer_2_out, multiplexer_4_out, multiplexer_5_out, register_1_q,
       register_2_q, register_3_q, register_4_q;

  Decoder #(.select(2), .disabled(0)) decoder_1 (
    .out0(decoder_1_out0), .out1(decoder_1_out1), .out2(decoder_1_out2), .out3(decoder_1_out3), .sel(WSEL),
    .en(WE));
  Register #(.width(32)) register_1 (.D(DATAIN), .en(decoder_1_out0), .Q(register_1_q), .clk(CLK), .clr(RST));
  Register #(.width(32)) register_2 (.D(DATAIN), .en(decoder_1_out1), .Q(register_2_q), .clk(CLK), .clr(RST));
  Register #(.width(32)) register_3 (.D(DATAIN), .en(decoder_1_out2), .Q(register_3_q), .clk(CLK), .clr(RST));
  Register #(.width(32)) register_4 (.D(DATAIN), .en(decoder_1_out3), .Q(register_4_q), .clk(CLK), .clr(RST));
  Multiplexer #(.width(32), .enable("false")) multiplexer_1 (
    .in0(register_1_q), .in1(register_2_q), .out(multiplexer_1_out), .sel(RSEL1[0]));
  Multiplexer #(.width(32), .enable("false")) multiplexer_2 (
    .in0(register_3_q), .in1(register_4_q), .out(multiplexer_2_out), .sel(RSEL1[0]));
  Multiplexer #(.width(32), .enable("false")) multiplexer_3 (
    .in0(multiplexer_1_out), .in1(multiplexer_2_out), .out(DATAOUT1), .sel(RSEL1[1]));
  Multiplexer #(.width(32), .enable("false")) multiplexer_4 (
    .in0(register_1_q), .in1(register_2_q), .out(multiplexer_4_out), .sel(RSEL2[0]));
  Multiplexer #(.width(32), .enable("false")) multiplexer_5 (
    .in0(register_3_q), .in1(register_4_q), .out(multiplexer_5_out), .sel(RSEL2[0]));
  Multiplexer #(.width(32), .enable("false")) multiplexer_6 (
    .in0(multiplexer_4_out), .in1(multiplexer_5_out), .out(DATAOUT2), .sel(RSEL2[1]));
endmodule

module REG16 (
  input  [3:0] in_1,
  input  [3:0] in_2,
  input  [3:0] in_3,
  input  in_4,
  input  [31:0] DATAIN,
  input  in_6,
  input  in_7,
  output [31:0] out_8,
  output [31:0] out_9
);

  wire decoder_1_out0, decoder_1_out1, decoder_1_out2, decoder_1_out3;
  wire [31:0] multiplexer_1_out, multiplexer_2_out, multiplexer_4_out, multiplexer_5_out, reg4_1_dataout1,
       reg4_1_dataout2, reg4_2_dataout1, reg4_2_dataout2, reg4_3_dataout1, reg4_3_dataout2, reg4_4_dataout1,
       reg4_4_dataout2;

  Decoder #(.select(2), .disabled(0)) decoder_1 (
    .out0(decoder_1_out0), .out1(decoder_1_out1), .out2(decoder_1_out2), .out3(decoder_1_out3),
    .sel(in_1[3:2]), .en(in_4));
  REG4 reg4_1 (
    .RSEL2(in_3[1:0]), .WE(decoder_1_out0), .RSEL1(in_2[1:0]), .WSEL(in_1[1:0]), .DATAIN(DATAIN),
    .DATAOUT1(reg4_1_dataout1), .DATAOUT2(reg4_1_dataout2), .CLK(in_6), .RST(in_7));
  REG4 reg4_2 (
    .RSEL2(in_3[1:0]), .WE(decoder_1_out1), .RSEL1(in_2[1:0]), .WSEL(in_1[1:0]), .DATAIN(DATAIN),
    .DATAOUT1(reg4_2_dataout1), .DATAOUT2(reg4_2_dataout2), .CLK(in_6), .RST(in_7));
  REG4 reg4_3 (
    .RSEL2(in_3[1:0]), .WE(decoder_1_out2), .RSEL1(in_2[1:0]), .WSEL(in_1[1:0]), .DATAIN(DATAIN),
    .DATAOUT1(reg4_3_dataout1), .DATAOUT2(reg4_3_dataout2), .CLK(in_6), .RST(in_7));
  REG4 reg4_4 (
    .RSEL2(in_3[1:0]), .WE(decoder_1_out3), .RSEL1(in_2[1:0]), .WSEL(in_1[1:0]), .DATAIN(DATAIN),
    .DATAOUT1(reg4_4_dataout1), .DATAOUT2(reg4_4_dataout2), .CLK(in_6), .RST(in_7));
  Multiplexer #(.width(32), .enable("false")) multiplexer_1 (
    .in0(reg4_1_dataout1), .in1(reg4_2_dataout1), .out(multiplexer_1_out), .sel(in_2[2]));
  Multiplexer #(.width(32), .enable("false")) multiplexer_2 (
    .in0(reg4_3_dataout1), .in1(reg4_4_dataout1), .out(multiplexer_2_out), .sel(in_2[2]));
  Multiplexer #(.width(32), .enable("false")) multiplexer_3 (
    .in0(multiplexer_1_out), .in1(multiplexer_2_out), .out(out_8), .sel(in_2[3]));
  Multiplexer #(.width(32), .enable("false")) multiplexer_4 (
    .in0(reg4_1_dataout2), .in1(reg4_2_dataout2), .out(multiplexer_4_out), .sel(in_3[2]));
  Multiplexer #(.width(32), .enable("false")) multiplexer_5 (
    .in0(reg4_3_dataout2), .in1(reg4_4_dataout2), .out(multiplexer_5_out), .sel(in_3[2]));
  Multiplexer #(.width(32), .enable("false")) multiplexer_6 (
    .in0(multiplexer_4_out), .in1(multiplexer_5_out), .out(out_9), .sel(in_3[3]));
endmodule

// REGS
module REG32 (
  input  [4:0] in_1,
  input  [4:0] in_2,
  input  [4:0] in_3,
  input  in_4,
  input  [31:0] in_5,
  input  in_6,
  input  in_7,
  output [31:0] out_8,
  output [31:0] out_9
);

  wire decoder_1_out0, decoder_1_out1;
  wire [31:0] reg16_1_out_8, reg16_1_out_9, reg16_2_out_8, reg16_2_out_9;

  Decoder #(.disabled(0)) decoder_1 (.out0(decoder_1_out0), .out1(decoder_1_out1), .sel(in_1[4]), .en(in_4));
  REG16 reg16_1 (
    .in_1(in_1[3:0]), .in_2(in_2[3:0]), .in_3(in_3[3:0]), .in_4(decoder_1_out0), .DATAIN(in_5),
    .out_8(reg16_1_out_8), .out_9(reg16_1_out_9), .in_6(in_6), .in_7(in_7));
  REG16 reg16_2 (
    .in_1(in_1[3:0]), .in_2(in_2[3:0]), .in_3(in_3[3:0]), .in_4(decoder_1_out1), .DATAIN(in_5),
    .out_8(reg16_2_out_8), .out_9(reg16_2_out_9), .in_6(in_6), .in_7(in_7));
  Multiplexer #(.width(32), .enable("false")) multiplexer_1 (
    .in0(reg16_1_out_8), .in1(reg16_2_out_8), .out(out_8), .sel(in_2[4]));
  Multiplexer #(.width(32), .enable("false")) multiplexer_2 (
    .in0(reg16_1_out_9), .in1(reg16_2_out_9), .out(out_9), .sel(in_3[4]));
endmodule

module ALU (
  input  [4:0] Sel,
  input  [31:0] A,
  input  [31:0] B,
  output [31:0] Result,
  output [2:0] Status
);

  wire comparator_2_eq;
  wire [0:0] and_2_out, and_3_out, comparator_2_gt, not_1_out;
  wire [31:0] adder_1_out, and_1_out, divider_1_out, divider_1_rem, multiplexer_1_out, multiplexer_2_out,
       multiplexer_3_out, multiplexer_4_out, multiplexer_5_out, multiplexer_6_out, multiplexer_7_out,
       multiplexer_8_out, multiplexer_9_out, multiplexer_10_out, multiplexer_11_out, multiplexer_12_out,
       multiplexer_13_out, multiplexer_14_out, multiplexer_15_out, multiplexer_16_out, multiplexer_17_out,
       multiplexer_18_out, multiplexer_19_out, multiplexer_20_out, multiplexer_21_out, multiplexer_22_out,
       multiplexer_23_out, multiplier_1_out, nor_1_out, or_1_out, shifter_1_out, shifter_2_out,
       shifter_3_out, subtractor_1_out, xnor_1_out, xor_1_out;

  Comparator #(.width(32)) comparator_1 (.a(A), .b(B), .gt(Status[1]), .eq(Status[0]));  // open: lt
  Comparator #(.width(32), .mode("unsigned")) comparator_2 (
    .a(A), .b(B), .gt(comparator_2_gt[0]), .eq(comparator_2_eq));  // open: lt
  assign nor_1_out = ~(A | B);  // NOR_Gate nor_1, 32 bits wide
  Shifter #(.width(32), .shift("ar")) shifter_1 (.in(A), .\dist (B[4:0]), .out(shifter_1_out));
  Multiplier #(.width(32)) multiplier_1 (.a(A), .b(B), .out(multiplier_1_out));  // open: cin, cout
  Divider #(.width(32)) divider_1 (.a(A), .b(B), .out(divider_1_out), .rem(divider_1_rem));  // open: upper
  Shifter #(.width(32), .shift("lr")) shifter_2 (.in(A), .\dist (B[4:0]), .out(shifter_2_out));
  assign xor_1_out = A ^ B;  // XOR_Gate xor_1, 32 bits wide
  assign and_1_out = A & B;  // AND_Gate and_1, 32 bits wide
  assign xnor_1_out = ~(A ^ B);  // XNOR_Gate xnor_1, 32 bits wide
  Adder #(.width(32)) adder_1 (.a(A), .b(B), .out(adder_1_out));  // open: cin, cout
  assign or_1_out = A | B;  // OR_Gate or_1, 32 bits wide
  Shifter #(.width(32)) shifter_3 (.in(A), .\dist (B[4:0]), .out(shifter_3_out));
  Subtractor #(.width(32)) subtractor_1 (.a(A), .b(B), .out(subtractor_1_out));  // open: bin, bout
  and and_2 (and_2_out[0], Status[0], Status[1]);
  and and_3 (and_3_out[0], comparator_2_gt[0], comparator_2_eq);
  not not_1 (not_1_out[0], comparator_2_eq);
  Multiplexer #(.width(32), .enable("false")) multiplexer_1 (
    .in0(nor_1_out), .in1(shifter_1_out), .out(multiplexer_1_out), .sel(Sel[0]));
  Multiplexer #(.width(32), .enable("false")) multiplexer_2 (
    .in0(multiplier_1_out), .in1(divider_1_out), .out(multiplexer_2_out), .sel(Sel[0]));
  Multiplexer #(.width(32), .enable("false")) multiplexer_3 (
    .in0(xor_1_out), .in1(divider_1_out), .out(multiplexer_3_out), .sel(Sel[0]));
  Multiplexer #(.width(32), .enable("false")) multiplexer_4 (
    .in0(and_1_out), .in1(xnor_1_out), .out(multiplexer_4_out), .sel(Sel[0]));
  Multiplexer #(.width(32), .enable("false")) multiplexer_5 (
    .in0(or_1_out), .in1(shifter_3_out), .out(multiplexer_5_out), .sel(Sel[0]));
  Multiplexer #(.width(32), .enable("false")) multiplexer_6 (
    .in0(and_1_out), .in1({{31{1'b0}}, Status[0]}), .out(multiplexer_6_out), .sel(Sel[0]));
  Multiplexer #(.width(32), .enable("false")) multiplexer_7 (
    .in0({{31{1'b0}}, Status[1]}), .in1({{31{1'b0}}, and_2_out[0]}), .out(multiplexer_7_out), .sel(Sel[0]));
  Multiplexer #(.width(32), .enable("false")) multiplexer_8 (
    .in0({{31{1'b0}}, and_3_out[0]}), .in1({{31{1'b0}}, comparator_2_gt[0]}), .out(multiplexer_8_out),
    .sel(Sel[0]));
  Multiplexer #(.width(32), .enable("false")) multiplexer_9 (
    .in0(or_1_out), .in1({{31{1'b0}}, not_1_out[0]}), .out(multiplexer_9_out), .sel(Sel[0]));
  Multiplexer #(.width(32), .enable("false")) multiplexer_10 (
    .in0(multiplexer_1_out), .in1(multiplexer_2_out), .out(multiplexer_10_out), .sel(Sel[1]));
  Multiplexer #(.width(32), .enable("false")) multiplexer_11 (
    .in0(shifter_2_out), .in1(multiplexer_3_out), .out(multiplexer_11_out), .sel(Sel[1]));
  Multiplexer #(.width(32), .enable("false")) multiplexer_12 (
    .in0(multiplexer_4_out), .in1(adder_1_out), .out(multiplexer_12_out), .sel(Sel[1]));
  Multiplexer #(.width(32), .enable("false")) multiplexer_13 (
    .in0(adder_1_out), .in1(multiplexer_5_out), .out(multiplexer_13_out), .sel(Sel[1]));
  Multiplexer #(.width(32), .enable("false")) multiplexer_14 (
    .in0(divider_1_rem), .in1(subtractor_1_out), .out(multiplexer_14_out), .sel(Sel[1]));
  Multiplexer #(.width(32), .enable("false")) multiplexer_15 (
    .in0(divider_1_rem), .in1(adder_1_out), .out(multiplexer_15_out), .sel(Sel[1]));
  Multiplexer #(.width(32), .enable("false")) multiplexer_16 (
    .in0(multiplexer_6_out), .in1(multiplexer_7_out), .out(multiplexer_16_out), .sel(Sel[1]));
  Multiplexer #(.width(32), .enable("false")) multiplexer_17 (
    .in0(multiplexer_8_out), .in1(multiplexer_9_out), .out(multiplexer_17_out), .sel(Sel[1]));
  Multiplexer #(.width(32), .enable("false")) multiplexer_18 (
    .in0(multiplexer_10_out), .in1(multiplexer_11_out), .out(multiplexer_18_out), .sel(Sel[2]));
  Multiplexer #(.width(32), .enable("false")) multiplexer_19 (
    .in0(multiplexer_12_out), .in1(multiplexer_13_out), .out(multiplexer_19_out), .sel(Sel[2]));
  Multiplexer #(.width(32), .enable("false")) multiplexer_20 (
    .in0(multiplexer_14_out), .in1(multiplexer_15_out), .out(multiplexer_20_out), .sel(Sel[2]));
  Multiplexer #(.width(32), .enable("false")) multiplexer_21 (
    .in0(multiplexer_16_out), .in1(multiplexer_17_out), .out(multiplexer_21_out), .sel(Sel[2]));
  Multiplexer #(.width(32), .enable("false")) multiplexer_22 (
    .in0(multiplexer_18_out), .in1(multiplexer_19_out), .out(multiplexer_22_out), .sel(Sel[3]));
  Multiplexer #(.width(32), .enable("false")) multiplexer_23 (
    .in0(multiplexer_20_out), .in1(multiplexer_21_out), .out(multiplexer_23_out), .sel(Sel[3]));
  Multiplexer #(.width(32), .enable("false")) multiplexer_24 (
    .in0(multiplexer_22_out), .in1(multiplexer_23_out), .out(Result), .sel(Sel[4]));

  assign Status[2] = 1'b0;

  // Notes on the sheet:
  //   Sel: pull=down
  //   MOD
  //   MOD
  //   AND
  //   OR
endmodule

module main (
);

  wire CLK, clock_1_out, demultiplexer_1_out0, demultiplexer_1_out1, demultiplexer_2_out0,
       demultiplexer_2_out1, INS_ERROR, MEM_ERROR, or_1_out, PCW, RST;
  wire [1:0] ADMX, ALUMX, fsm_1_out_2, fsm_1_out_3, fsm_1_out_4, fsm_1_out_5, MLEN, RWDMX;
  wire [2:0] fsm_1_out_6;
  wire [4:0] multiplexer_4_out, multiplexer_7_out;
  wire [9:0] alu_1_status;
  wire [30:0] fsm_1_out;
  wire [31:0] adder_1_out, ALUR, controlled_buffer_1_out, IR_q, multiplexer_1_out, multiplexer_2_out,
       multiplexer_3_out, multiplexer_5_out, multiplexer_6_out, PC_q, PCBUFF_q, reg32_1_out_9, REGS1,
       shifter_1_out, sign_ext16_1_out, sign_ext26_1_out;

  Clock clock_1 (.out(clock_1_out));
  Pull_Resistor pull_resistor_1 (.node(RST));
  Multiplexer #(.select(2), .width(32), .enable("false")) multiplexer_1 (
    .in0(adder_1_out), .in1(REGS1), .in2(ALUR), .out(multiplexer_1_out), .sel(fsm_1_out[7:6]));  // open: in3
  Button button_1 (.out(RST));
  or or_1 (or_1_out, INS_ERROR, MEM_ERROR);
  and and_1 (CLK, ~or_1_out, clock_1_out);  // AND_Gate
  Multiplexer #(.select(2), .width(32), .enable("false")) multiplexer_2 (
    .in0(PC_q), .in1(ALUR), .out(multiplexer_2_out), .sel(ADMX));  // open: in2, in3
  Register #(.width(32)) PC (.D(multiplexer_1_out), .en(PCW), .Q(PC_q), .clk(CLK), .clr(RST));
  Register #(.width(32)) IR (.D(controlled_buffer_1_out), .en(fsm_1_out[30]), .Q(IR_q), .clk(CLK), .clr(RST));
  Adder #(.width(32)) adder_1 (.a(PC_q), .b(32'h4), .out(adder_1_out));  // open: cin, cout
  Multiplexer #(.select(2), .width(32), .enable("false")) multiplexer_3 (
    .in0(controlled_buffer_1_out), .in1(ALUR), .in2(PC_q), .out(multiplexer_3_out), .sel(RWDMX));  // open: in3
  Pull_Resistor pull_resistor_2 (.node(fsm_1_out[26]));
  SIGN_EXT26 sign_ext26_1 (.IN(IR_q), .OUT(sign_ext26_1_out));
  Multiplexer #(.select(2), .width(5), .enable("false")) multiplexer_4 (
    .in0(IR_q[15:11]), .in1(IR_q[20:16]), .in2(5'b11101), .out(multiplexer_4_out), .sel(fsm_1_out_2));  // open: in3
  REG32 reg32_1 (
    .in_1(multiplexer_4_out), .in_2(IR_q[25:21]), .in_3(IR_q[20:16]), .in_4(fsm_1_out[26]), .out_8(REGS1),
    .in_5(multiplexer_3_out), .out_9(reg32_1_out_9), .in_6(CLK), .in_7(RST));
  LED u_INS_ERROR (.in(INS_ERROR));
  LED RESET (.in(RST));
  LED u_MEM_ERROR (.in(MEM_ERROR));
  Pull_Resistor pull_resistor_3 (.node(fsm_1_out[28]));
  Pull_Resistor pull_resistor_4 (.node(fsm_1_out[29]));
  assign controlled_buffer_1_out = fsm_1_out[29] ? reg32_1_out_9 : 32'bz;  // Controlled_Buffer controlled_buffer_1
  Demultiplexer #(.select(2), .enable("false")) demultiplexer_1 (
    .out0(demultiplexer_1_out0), .out1(demultiplexer_1_out1), .in(fsm_1_out[28]),
    .sel(multiplexer_2_out[19:18]));  // open: out2, out3
  SDRAM sdram_1 (
    .ADDR(multiplexer_2_out[17:0]), .LEN(MLEN), .DIN(controlled_buffer_1_out),
    .DOUT(controlled_buffer_1_out), .ERROR(MEM_ERROR), .STR(demultiplexer_1_out0), .CLK(CLK),
    .LD(demultiplexer_2_out0));
  Demultiplexer #(.select(2), .enable("false")) demultiplexer_2 (
    .out0(demultiplexer_2_out0), .out1(demultiplexer_2_out1), .in(fsm_1_out[27]),
    .sel(multiplexer_2_out[19:18]));  // open: out2, out3
  Register #(.width(32)) PCBUFF (.D(PC_q), .en(PCW), .Q(PCBUFF_q), .clk(CLK));  // open: clr
  SIGN_EXT16 sign_ext16_1 (.IN(IR_q[15:0]), .SIGN(fsm_1_out[24]), .OUT(sign_ext16_1_out));
  FSM fsm_1 (
    .IN({IR_q[31:26], alu_1_status}), .ERROR(INS_ERROR), .CLK(CLK), .RST(RST),
    .OUT({PCW, fsm_1_out[30:23], fsm_1_out_6, fsm_1_out_5, fsm_1_out_4, fsm_1_out_3, MLEN, ALUMX, ADMX, fsm_1_out[7:6], RWDMX, fsm_1_out_2, fsm_1_out[1:0]}));
  Pull_Resistor pull_resistor_5 (.node(fsm_1_out[27]));
  Multiplexer #(.width(32), .enable("false")) multiplexer_5 (
    .in0(PCBUFF_q), .in1(REGS1), .out(multiplexer_5_out), .sel(fsm_1_out[25]));
  Multiplexer #(.select(2), .width(32), .enable("false")) multiplexer_6 (
    .in0(reg32_1_out_9), .in1(sign_ext16_1_out), .in2({IR_q[15:0], {16{1'b0}}}), .in3(sign_ext26_1_out),
    .out(multiplexer_6_out), .sel(fsm_1_out[1:0]));
  Shifter #(.width(32)) shifter_1 (.in(multiplexer_6_out), .\dist ({3'b000, fsm_1_out[23], 1'b0}), .out(shifter_1_out));
  Multiplexer #(.select(2), .width(5), .disabled(0), .enable("false")) multiplexer_7 (
    .in0(IR_q[30:26]), .in1(5'b01101), .out(multiplexer_7_out), .sel(ALUMX));  // open: in2, in3
  // Probe on ALUR
  ALU alu_1 (
    .A(multiplexer_5_out), .B(shifter_1_out), .Sel(multiplexer_7_out), .Result(ALUR),
    .Status(alu_1_status[2:0]));
  // Probe on alu_1_status[2:0]
  PERIPH periph_1 (
    .ADDR(multiplexer_2_out[17:0]), .DIN(controlled_buffer_1_out), .STR(demultiplexer_1_out1),
    .LD(demultiplexer_2_out1), .CLK(CLK), .RST(RST));  // open: DOUT

  // Notes on the sheet:
  //   CLK
  //   Address bus
  //   Data bus
  //   RST
  //   RA
  //   control FSM output
  //   ROP2 or RIDEST
  //   IMMEDIATE
  //   RRDEST
  //   ROP1
  //   OPCODE
  //   IMM
  //   MAIN SDRAM
  //   control FSM input
  //   ADD
endmodule

module BRANCH (
  input  op2,
  input  op3,
  input  op4,
  input  sta0,
  input  sta1,
  input  sta2,
  output branch
);

  wire and_1_out, and_2_out, and_3_out, and_4_out, and_5_out, and_6_out, and_7_out, not_1_out, not_2_out,
       not_3_out, not_4_out, not_5_out, not_6_out, not_7_out, not_8_out, not_9_out;

  not not_1 (not_1_out, op2);
  not not_2 (not_2_out, op3);
  not not_3 (not_3_out, op4);
  not not_4 (not_4_out, op4);
  not not_5 (not_5_out, op2);
  not not_6 (not_6_out, sta0);
  not not_7 (not_7_out, op3);
  not not_8 (not_8_out, op4);
  not not_9 (not_9_out, sta0);
  and and_1 (and_1_out, not_1_out, not_2_out, not_3_out);
  and and_2 (and_2_out, not_4_out, sta1);
  and and_3 (and_3_out, not_5_out, op4, sta0);
  and and_4 (and_4_out, op3, not_6_out, sta1);
  and and_5 (and_5_out, op2, not_7_out, sta1);
  and and_6 (and_6_out, op2, not_8_out, sta0);
  and and_7 (and_7_out, op2, op3, not_9_out);
  or or_1 (branch, and_1_out, and_2_out, and_3_out, and_4_out, and_5_out, and_6_out, and_7_out);
endmodule

module TRANS (
  input  IS_ALU,
  input  IS_MEM,
  input  IS_BRANCH,
  input  BRANCH,
  output ad0,
  output ad1,
  output ad2,
  output ad3,
  output error
);

  wire and_1_out, and_2_out, and_3_out, and_4_out, and_5_out, and_6_out, and_7_out, not_1_out, not_2_out,
       not_3_out, not_4_out, not_5_out, not_6_out, not_7_out, not_8_out, not_9_out, not_10_out;

  not not_1 (not_1_out, IS_ALU);
  and and_1 (and_1_out, not_1_out, not_2_out);
  not not_2 (not_2_out, IS_BRANCH);
  not not_3 (not_3_out, IS_ALU);
  and and_2 (and_2_out, not_3_out, BRANCH);
  not not_4 (not_4_out, IS_ALU);
  and and_3 (and_3_out, not_4_out, IS_MEM);
  not not_5 (not_5_out, IS_BRANCH);
  or or_1 (ad1, not_5_out, IS_MEM, IS_ALU);
  not not_6 (not_6_out, IS_ALU);
  not not_7 (not_7_out, IS_MEM);
  not not_8 (not_8_out, IS_ALU);
  not not_9 (not_9_out, IS_MEM);
  and and_4 (and_4_out, not_8_out, not_9_out, not_10_out);
  not not_10 (not_10_out, IS_BRANCH);
  and and_5 (and_5_out, IS_MEM, IS_BRANCH);
  and and_6 (and_6_out, IS_ALU, IS_BRANCH);
  and and_7 (and_7_out, IS_ALU, IS_MEM);
  or or_2 (ad0, and_1_out, and_2_out, and_3_out);
  and and_8 (ad2, not_6_out, not_7_out, IS_BRANCH, BRANCH);
  or or_3 (error, and_4_out, and_5_out, and_6_out, and_7_out);

  assign ad3 = 1'b0;
endmodule

// EXT
module SIGN_EXT16 (
  input  [15:0] IN,
  input  SIGN,
  output [31:0] OUT
);

  wire and_1_out;

  and and_1 (and_1_out, IN[15], SIGN);
  Multiplexer #(.width(32), .disabled(0), .enable("false")) multiplexer_1 (
    .in0({{16{1'b0}}, IN}), .in1({{16{1'b1}}, IN}), .out(OUT), .sel(and_1_out));
endmodule

module SDRAM (
  input  [17:0] ADDR,
  input  STR,
  input  CLK,
  input  LD,
  input  [1:0] LEN,
  input  [31:0] DIN,
  output [31:0] DOUT,
  output ERROR
);

  wire ramdec_1_mxin0, ramdec_1_mxin1, ramdec_1_mxin2, ramdec_1_mxin3;
  wire [1:0] multiplexer_2_out, not_2_out;
  wire [1:1] not_1_out;
  wire [7:0] ram_1_data, ram_1_data_2, ram_1_data_3, ram_1_data_4;
  wire [31:0] and_1_out, and_2_out, MASK, multiplexer_6_out, shifter_1_out, shifter_2_out;

  Multiplexer #(.select(2), .width(32), .disabled(0), .enable("false")) multiplexer_1 (
    .in0({32{1'b1}}), .in1(32'hffff), .in2(32'hff), .out(MASK), .sel(LEN));  // open: in3
  // Probe on DIN
  not not_1 (not_1_out[1], ADDR[1]);
  assign not_2_out = ~ADDR[1:0];  // NOT_Gate not_2, 2 bits wide
  assign and_1_out = MASK & DIN;  // AND_Gate and_1, 32 bits wide
  Shifter #(.width(32)) shifter_1 (.in(and_1_out), .\dist ({multiplexer_2_out, 3'b000}), .out(shifter_1_out));
  Multiplexer #(.select(2), .width(2), .disabled(0), .enable("false")) multiplexer_2 (
    .in0(2'b00), .in1({not_1_out[1], 1'b0}), .in2(not_2_out), .out(multiplexer_2_out), .sel(LEN));  // open: in3
  Multiplexer #(.width(8), .disabled(0), .enable("false")) multiplexer_3 (
    .in0(shifter_1_out[31:24]), .in1(ram_1_data_4), .out(multiplexer_6_out[31:24]), .sel(ramdec_1_mxin0));
  RAMDEC ramdec_1 (
    .LEN1(LEN[1]), .LEN0(LEN[0]), .AD1(ADDR[1]), .AD0(ADDR[0]), .MXIN0(ramdec_1_mxin0),
    .MXIN1(ramdec_1_mxin1), .MXIN2(ramdec_1_mxin2), .MXIN3(ramdec_1_mxin3), .ERROR(ERROR));
  Multiplexer #(.width(8), .disabled(0), .enable("false")) multiplexer_4 (
    .in0(shifter_1_out[23:16]), .in1(ram_1_data_3), .out(multiplexer_6_out[23:16]), .sel(ramdec_1_mxin1));
  Multiplexer #(.width(8), .disabled(0), .enable("false")) multiplexer_5 (
    .in0(shifter_1_out[15:8]), .in1(ram_1_data_2), .out(multiplexer_6_out[15:8]), .sel(ramdec_1_mxin2));
  Multiplexer #(.width(8), .disabled(0), .enable("false")) multiplexer_6 (
    .in0(shifter_1_out[7:0]), .in1(ram_1_data), .out(multiplexer_6_out[7:0]), .sel(ramdec_1_mxin3));
  RAM #(.addrWidth(16), .dataWidth(32), .bus("separate")) ram_1 (
    .addr(ADDR[17:2]), .din(multiplexer_6_out),
    .data({ram_1_data_4, ram_1_data_3, ram_1_data_2, ram_1_data}), .str(STR), .sel(1'b1), .clk(CLK), .ld(1'b1));  // open: clr
  Shifter #(.width(32), .shift("lr")) shifter_2 (
    .in({ram_1_data_4, ram_1_data_3, ram_1_data_2, ram_1_data}), .\dist ({multiplexer_2_out, 3'b000}),
    .out(shifter_2_out));
  assign DOUT = LD ? and_2_out : 32'bz;  // Controlled_Buffer controlled_buffer_1
  assign and_2_out = shifter_2_out & MASK;  // AND_Gate and_2, 32 bits wide
endmodule

module RAMDEC (
  input  LEN1,
  input  LEN0,
  input  AD1,
  input  AD0,
  output MXIN0,
  output MXIN1,
  output MXIN2,
  output MXIN3,
  output ERROR
);

  wire and_1_out, and_2_out, and_3_out, and_4_out, and_5_out, and_6_out, and_7_out, and_8_out, and_9_out,
       and_10_out, and_11_out, and_12_out, and_13_out, and_14_out, and_15_out, and_16_out, and_17_out,
       and_18_out, and_19_out, and_20_out, and_21_out, not_1_out, not_2_out, not_3_out, not_4_out, not_5_out,
       not_6_out, not_7_out, not_8_out, not_9_out;

  and and_1 (and_1_out, LEN0, AD0);
  and and_2 (and_2_out, LEN0, AD1);
  and and_3 (and_3_out, LEN1, AD0);
  and and_4 (and_4_out, LEN1, AD1);
  and and_5 (and_5_out, LEN1, LEN0);
  and and_6 (and_6_out, LEN0, AD0);
  and and_7 (and_7_out, LEN0, AD1);
  and and_8 (and_8_out, LEN1, not_1_out);
  not not_1 (not_1_out, AD0);
  and and_9 (and_9_out, LEN1, AD1);
  and and_10 (and_10_out, LEN0, not_2_out);
  not not_2 (not_2_out, AD1);
  and and_11 (and_11_out, LEN0, AD0);
  and and_12 (and_12_out, LEN1, not_3_out);
  not not_3 (not_3_out, AD1);
  and and_13 (and_13_out, LEN1, AD0);
  and and_14 (and_14_out, LEN1, LEN0);
  and and_15 (and_15_out, LEN0, not_4_out);
  not not_4 (not_4_out, AD1);
  and and_16 (and_16_out, LEN0, AD0);
  and and_17 (and_17_out, LEN1, not_5_out);
  not not_5 (not_5_out, AD1);
  and and_18 (and_18_out, LEN1, not_6_out);
  not not_6 (not_6_out, AD0);
  not not_7 (not_7_out, LEN1);
  and and_19 (and_19_out, not_7_out, AD0);
  not not_8 (not_8_out, LEN1);
  not not_9 (not_9_out, LEN0);
  and and_20 (and_20_out, not_8_out, not_9_out, AD1);
  and and_21 (and_21_out, LEN1, LEN0);
  or or_1 (MXIN0, and_1_out, and_2_out, and_3_out, and_4_out, and_5_out);
  or or_2 (MXIN1, and_6_out, and_7_out, and_8_out, and_9_out);
  or or_3 (MXIN2, and_10_out, and_11_out, and_12_out, and_13_out, and_14_out);
  or or_4 (MXIN3, and_15_out, and_16_out, and_17_out, and_18_out);
  or or_5 (ERROR, and_19_out, and_20_out, and_21_out);
endmodule

// EXT
module SIGN_EXT26 (
  input  [31:0] IN,
  output [31:0] OUT
);

  Multiplexer #(.width(32), .disabled(0), .enable("false")) multiplexer_1 (
    .in0({{6{1'b0}}, IN[25:0]}), .in1({{6{1'b1}}, IN[25:0]}), .out(OUT), .sel(IN[25]));
endmodule

module PERIPH (
  input  [17:0] ADDR,
  input  [31:0] DIN,
  input  STR,
  input  LD,
  input  CLK,
  input  RST,
  output [31:0] DOUT
);

  wire decoder_1_out0, decoder_1_out1, decoder_1_out2, decoder_1_out3, demultiplexer_1_out0,
       demultiplexer_1_out1, register_1_q, register_2_q, register_3_q, register_4_q;

  Demultiplexer #(.select(2), .enable("false")) demultiplexer_1 (
    .out0(demultiplexer_1_out0), .out1(demultiplexer_1_out1), .in(STR), .sel(ADDR[5:4]));  // open: out2, out3
  Demultiplexer #(.select(2), .enable("false")) demultiplexer_2 (
    .in(LD), .sel(ADDR[5:4]));  // open: out0, out1, out2, out3
  Decoder #(.select(2), .disabled(0)) decoder_1 (
    .out0(decoder_1_out0), .out1(decoder_1_out1), .out2(decoder_1_out2), .out3(decoder_1_out3),
    .sel(ADDR[1:0]), .en(demultiplexer_1_out0));
  // Probe on DIN[6:0]
  TTY tty_1 (.data(DIN[6:0]), .clk(CLK), .we(demultiplexer_1_out1), .clr(RST));
  // Probe on demultiplexer_1_out1
  LED led_1 (.in(register_1_q));
  Register #(.width(1)) register_1 (.D(DIN[0]), .en(decoder_1_out0), .Q(register_1_q), .clk(CLK), .clr(RST));
  Register #(.width(1)) register_2 (.D(DIN[0]), .en(decoder_1_out1), .Q(register_2_q), .clk(CLK), .clr(RST));
  Keyboard keyboard_1 ();  // open: clk, re, clr, avail, data
  LED led_2 (.in(register_3_q));
  LED led_3 (.in(register_2_q));
  Register #(.width(1)) register_3 (.D(DIN[0]), .en(decoder_1_out2), .Q(register_3_q), .clk(CLK), .clr(RST));
  LED led_4 (.in(register_4_q));
  Register #(.width(1)) register_4 (.D(DIN[0]), .en(decoder_1_out3), .Q(register_4_q), .clk(CLK), .clr(RST));
endmodule
